# Fritzing sketch Untitled Sketch (saved by Fritzing 0.9.4)
breadboards: 1

parts:
  U1 = atmega328 [package=dip]
  XTAL1 = Crystal [frequency="16 Mhz" package=SMD]
  R1 = Resistor [tolerance=±5% resistance=220 package="1206 [SMD]"]
  Part4 = Humidity Temperature Sensor SHT15
  Part5 = Humidity Temperature Sensor SHT15
  Part6 = NRF24L01+ Breakout Board

nets:
  N1: U1.RESET, R1.Pin_1
  VCC: U1.VCC, U1.AVCC, R1.Pin_0, Part4.VCC, Part5.VCC, Part6.VCC
  GND: U1.GND, Part4.GND, Part5.GND, Part6.GND
  N2: U1.XLAT1, XTAL1.pin_0
  N3: U1.XLAT2, XTAL1.pin_1
  N4: U1.D8, Part6.CE
  N5: U1.D10_(PWM), Part6.CS
  N6: U1.D11_(PWM), Part6.MOSI
  N7: U1.D12, Part6.MISO
  N8: U1.D13, Part6.SCK
  N9: U1.A4, Part4.SDA
  N10: U1.A5, Part4.SCL
